# Fritzing sketch sms (saved by Fritzing 0.9.3b)
breadboards: 2

parts:
  IC1 = PICAXE-20M [package=THT]
  R3 = Resistor [tolerance=±5% resistance=270 package=THT]
  R4 = Resistor [tolerance=±5% resistance=10k package=THT]
  R5 = Trimmer Potentiometer [maximum_resistance=50kΩ package=THT]
  Part1 = Adafruit T-Cobbler Plus [part_number="Adafruit #1989 and #2028"]
  R6 = Resistor [tolerance=±5% resistance=270 package=THT]
  R7 = Resistor [tolerance=±5% resistance=270 package=THT]
  LED4 = LED - 5mm [color="Red (633nm)" package="5 mm [THT]"]
  LED5 = LED - 5mm [color="Red (633nm)" package="5 mm [THT]"]
  LED6 = LED - 5mm [color="Red (633nm)" package="5 mm [THT]"]
  S2 = Pushbutton [package="[THT]"]
  R8 = Resistor [tolerance=±5% resistance=270 package=THT]
  LED7 = LED - 5mm [color="Red (633nm)" package="5 mm [THT]"]

nets:
  N1: IC1.+V, R4.Pin_0, R5.leg2, Part1.+3.3V
  N2: IC1.In_1_/_ADC_1, R5.wiper
  N3: IC1.Out_3, Part1.GPIO19
  N4: IC1.Out_2, Part1.GPIO5
  N5: IC1.Out_1, Part1.GPIO22
  N6: IC1.Out_0_/_Infraout, Part1.GPIO27
  N7: IC1.0V, R3.Pin_0, R5.leg1, Part1.GND, R6.Pin_0, R7.Pin_0, S2.Pin_1, S2.Pin_2, R8.Pin_0
  N8: R3.Pin_1, LED5.cathode
  N9: R4.Pin_1, Part1.GPIO25, S2.Pin_3, S2.Pin_4
  N10: Part1.GPIO23, LED5.anode
  N11: Part1.GPIO24, LED4.anode
  N12: Part1.GPIO20, LED7.anode
  N13: Part1.GPIO21, LED6.anode
  N14: R6.Pin_1, LED4.cathode
  N15: R7.Pin_1, LED6.cathode
  N16: R8.Pin_1, LED7.cathode

custom parts:
  Adafruit T-Cobbler Plus: The Raspberry Pi has landed on the Maker World like a 40-GPIO pinned, quad-USB ported, credit card sized bomb of DIY joy. And while you can use most of our great Model B accessories by hooking up our downgrade cable, its probably a good time to upgrade your set up and accessorize using all of the 40 pins. That's why we now carry the Assembled Adafruit Pi T-Cobbler Plus - Breakout + Cable for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
